# Fritzing sketch circuit (saved by Fritzing 0.9.4)
circuit board: 8.46667cm x 5.64444cm
breadboards: 1

parts:
  Pro_Micro1 = SparkFun Pro Micro
  R_POT2 = Rotary Potentiometer (Small) [maximum_resistance=100kΩ package=THT]
  LED_POT2 = LEDs [package=led10mm]
  LED_POT1 = LEDs [package=led10mm]
  LED_MUTE = LEDs [package=led10mm]
  LED_RGB = RGB LED (com. anode, rbg) [package="5 mm [THT]"]
  R_LED = Resistor [tolerance=±5% resistance=220 package="1206 [SMD]"]
  R_LED_2 = Resistor [tolerance=±5% resistance=220 package="1206 [SMD]"]
  R_LED_3 = Resistor [tolerance=±5% resistance=220 package="1206 [SMD]"]
  R_RGB = Resistor [tolerance=±5% resistance=10k package="1206 [SMD]"]
  R_RGB_2 = Resistor [tolerance=±5% resistance=10k package="1206 [SMD]"]
  R_RGB_3 = Resistor [tolerance=±5% resistance=10k package="1206 [SMD]"]
  S3 = Pushbutton [package=THT]
  U1 = SWITCH_SPDT [package=kps-1290]
  R_POT1 = Rotary Potentiometer (Small) [maximum_resistance=100kΩ package=THT]

nets:
  N1: Pro_Micro1.GND, R_POT2.leg2, R_LED.Pin_1, R_LED_2.Pin_1, R_LED_3.Pin_1, S3.leg1, U1.P, R_POT1.leg2
  N2: Pro_Micro1.3, Pro_Micro1.4, LED_POT2.A, LED_POT1.A
  N3: Pro_Micro1.5, LED_MUTE.A
  N4: Pro_Micro1.7, R_RGB.Pin_1
  N5: Pro_Micro1.8, R_RGB_2.Pin_1
  N6: Pro_Micro1.9, R_RGB_3.Pin_1
  N7: Pro_Micro1.10, S3.leg0
  N8: Pro_Micro1.16, U1.O
  N9: Pro_Micro1.A0, R_POT1.wiper
  N10: Pro_Micro1.A1, R_POT2.wiper
  N11: Pro_Micro1.VCC, R_POT2.leg1, LED_RGB.common_anode, R_POT1.leg1
  N12: LED_POT2.C, R_LED.Pin_0
  N13: LED_POT1.C, R_LED_2.Pin_0
  N14: LED_MUTE.C, R_LED_3.Pin_0
  N15: LED_RGB.red_cathode, R_RGB.Pin_0
  N16: LED_RGB.blue_cathode, R_RGB_2.Pin_0
  N17: LED_RGB.green_cathode, R_RGB_3.Pin_0

custom parts:
  SparkFun Pro Micro: The Pro Micro is similar to the Pro Mini except with an ATmega32U4 on board. The USB transceiver inside the 32U4 allows us to add USB connectivity on-board and do away with bulky external USB interface. Based on: https://github.com/unorthodox-engineers/unorthodox-arduino/blob/master/Unorthodox/fritzing/parts/Pro%20Micro.fzpz
